# Fritzing sketch fulldefence (saved by Fritzing 0.9.3b)
breadboards: 4

parts:
  Transceiver1 = nRF24L01 [package=module]
  R1 = Rotary Potentiometer (Large) [maximum_resistance=100kΩ package=THT]
  R2 = Rotary Potentiometer (Large) [maximum_resistance=100kΩ package=THT]
  Part1 = Arduino Uno (Rev3)
  VCC1 = Battery block 9V  # not connected
  Part2 = Arduino Uno (Rev3)
  VCC2 = Battery block 9V  # not connected
  Transceiver2 = nRF24L01 [package=module]
  J1 = Basic Servo
  J2 = Basic Servo
  U1 = ENCODER-QUADRATURE [package=encoder-16mm-quad]
  S1 = Toggle Switch [package=THT]
  S2 = Toggle Switch [package=THT]
  S3 = Toggle Switch [package=THT]
  S4 = Toggle Switch [package=THT]
  S5 = Toggle Switch [package=THT]
  S6 = Toggle Switch [package=THT]
  S7 = Toggle Switch [package=THT]
  R3 = Resistor [tolerance=±5% resistance=10k package="0805 [SMD]"]
  R4 = Resistor [tolerance=±5% resistance=10k package="0805 [SMD]"]
  R5 = Resistor [tolerance=±5% resistance=10k package="0805 [SMD]"]
  R6 = Resistor [tolerance=±5% resistance=10k package="0805 [SMD]"]
  R7 = Resistor [tolerance=±5% resistance=10k package="0805 [SMD]"]
  R8 = Resistor [tolerance=±5% resistance=10k package="0805 [SMD]"]
  R9 = Resistor [tolerance=±5% resistance=10k package="0805 [SMD]"]
  L1 = Solenoid
  L2 = Solenoid
  L3 = Solenoid
  L4 = Solenoid
  L5 = Solenoid
  L6 = Solenoid
  L7 = Solenoid
  J3 = Basic Servo
  D1 = Rectifier Diode 10A [part_number=P1000K]
  Q1 = npn-Powertransistor [package="TO220 [THT]"]
  Q2 = npn-Powertransistor [package="TO220 [THT]"]
  Q3 = npn-Powertransistor [package="TO220 [THT]"]
  Q4 = npn-Powertransistor [package="TO220 [THT]"]
  Q5 = npn-Powertransistor [package="TO220 [THT]"]
  Q6 = npn-Powertransistor [package="TO220 [THT]"]
  Q7 = npn-Powertransistor [package="TO220 [THT]"]
  D2 = Rectifier Diode 10A [part_number=P1000K]
  D3 = Rectifier Diode 10A [part_number=P1000K]
  D4 = Rectifier Diode 10A [part_number=P1000K]
  D5 = Rectifier Diode 10A [part_number=P1000K]
  D6 = Rectifier Diode 10A [part_number=P1000K]
  D7 = Rectifier Diode 10A [part_number=P1000K]
  R11 = Resistor [tolerance=±5% resistance=220 package=THT]
  R12 = Resistor [tolerance=±5% resistance=220 package=THT]
  R13 = Resistor [tolerance=±5% resistance=220 package=THT]
  R14 = Resistor [tolerance=±5% resistance=220 package=THT]
  R15 = Resistor [tolerance=±5% resistance=220 package=THT]
  R16 = Resistor [tolerance=±5% resistance=220 package=THT]
  R17 = Resistor [tolerance=±5% resistance=220 package=THT]

nets:
  GND: Transceiver1.GND, R1.leg1, R2.leg1, Part1.GND, U1.C
  VCC: Transceiver1.VCC, Part1.3V3
  N1: Transceiver1.CE, Part1.D9_PWM
  N2: Transceiver1.CSN, Part1.D10_PWM/SS
  N3: Transceiver1.SCK, Part1.D13/SCK
  N4: Transceiver1.MOSI, Part1.D11_PWM/MOSI
  N5: Transceiver1.MISO, Part1.D12/MISO
  N6: R1.wiper, Part1.A1
  N7: R1.leg2, R2.leg2, Part1.5V, U1.A, S1.COM, S2.COM, S3.COM, S4.COM, S5.COM, S6.COM, S7.COM
  N8: R2.wiper, Part1.A2
  N9: Part1.A0, S6.L1, R9.Pin_1
  N10: Part1.A3, U1.B
  N11: Part1.D8, S7.L1, R6.Pin_1
  N12: Part1.D3_PWM, S1.L1, R4.Pin_1
  N13: Part1.D4, S2.L1, R3.Pin_1
  N14: Part1.D5_PWM, S3.L1, R7.Pin_1
  N15: Part1.D6_PWM, S4.L1, R5.Pin_1
  N16: Part1.D7, S5.L1, R8.Pin_1
  N17: Part2.A0, R17.Pin_0
  N18: Part2.A1, R16.Pin_0
  N19: Part2.A2, R15.Pin_0
  N20: Part2.A3, R14.Pin_0
  N21: Part2.A4/SDA, R13.Pin_0
  N22: Part2.A5/SCL, R12.Pin_0
  N23: Part2.D9_PWM, Transceiver2.CE
  N24: Part2.D10_PWM/SS, Transceiver2.CSN
  N25: Part2.D11_PWM/MOSI, Transceiver2.MOSI
  N26: Part2.D12/MISO, Transceiver2.MISO
  N27: Part2.D13/SCK, Transceiver2.SCK
  GND_2: Part2.GND, Transceiver2.GND, J1.gnd, J2.gnd, J3.gnd, Q1.emitter, Q2.emitter, Q3.emitter, Q4.emitter, Q5.emitter, Q6.emitter, Q7.emitter
  N28: Part2.D3_PWM, J3.pulse
  N29: Part2.D5_PWM, J2.pulse
  N30: Part2.D6_PWM, J1.pulse
  N31: Part2.D7, R11.Pin_0
  3V3: Part2.3V3, Transceiver2.VCC
  VCC_2: Part2.5V, J1.vcc, J2.vcc, L1.pin2, L2.pin2, L3.pin2, L4.pin2, L5.pin2, L6.pin2, L7.pin2, J3.vcc, D1.cathode, D2.cathode, D3.cathode, D4.cathode, D5.cathode, D6.cathode, D7.cathode
  N32: L2.pin1, Q3.collector, D3.anode
  N33: L3.pin1, Q6.collector, D6.anode
  N34: L4.pin1, Q5.collector, D5.anode
  N35: L5.pin1, D1.anode, Q1.collector
  N36: L6.pin1, Q2.collector, D2.anode
  N37: L7.pin1, Q4.collector, D4.anode
  N38: Q1.base, R11.Pin_1
  N39: Q2.base, R12.Pin_1
  N40: Q3.base, R13.Pin_1
  N41: Q4.base, R14.Pin_1
  N42: Q5.base, R15.Pin_1
  N43: Q6.base, R16.Pin_1
  N44: Q7.base, R17.Pin_1
  N45: Q7.collector, D7.anode

custom parts:
  nRF24L01: nRF24L01 module
